# Fritzing sketch component (saved by Fritzing 0.9.3b)
breadboards: 3
perfboards: 3

parts:
  Raspberry_Pi_1 = Raspberry Pi 3 [part_number=RPI-3-V1.2]
  U1 = 74HC595 [package="DIP16 [THT]"]
  LED1 = LED - 5mm [color="Green (555nm)" package="5 mm [THT]"]
  LED2 = LED - 5mm [color="Green (555nm)" package="5 mm [THT]"]
  LED3 = LED - 5mm [color="Green (555nm)" package="5 mm [THT]"]
  LED4 = LED - 5mm [color="Green (555nm)" package="5 mm [THT]"]
  LED5 = LED - 5mm [color="Green (555nm)" package="5 mm [THT]"]
  LED6 = LED - 5mm [color="Green (555nm)" package="5 mm [THT]"]
  LED7 = LED - 5mm [color="Green (555nm)" package="5 mm [THT]"]
  LED8 = LED - 5mm [color="Green (555nm)" package="5 mm [THT]"]
  LED9 = LED - 5mm [color="Green (555nm)" package="5 mm [THT]"]
  LED10 = LED - 5mm [color="Green (555nm)" package="5 mm [THT]"]
  LED11 = LED - 5mm [color="Yellow (592nm)" package="5 mm [THT]"]
  LED12 = LED - 5mm [color="Yellow (592nm)" package="5 mm [THT]"]
  LED13 = LED - 5mm [color="Yellow (592nm)" package="5 mm [THT]"]
  LED14 = LED - 5mm [color="Yellow (592nm)" package="5 mm [THT]"]
  LED15 = LED - 5mm [color="Red (635nm)" package="5 mm [THT]"]
  LED16 = LED - 5mm [color="Red (635nm)" package="5 mm [THT]"]
  R40 = Resistor [tolerance=±5% resistance=1k package=THT]
  R42 = Resistor [tolerance=±5% resistance=1k package=THT]
  R47 = Resistor [tolerance=±5% resistance=4.7k package=THT]
  IC1 = IC, DIP package, 16 pins [chip_label=74LS47]
  7_Segment1 = 7 Segment Display  # not connected
  S1 = Pushbutton [package="[THT]"]
  U2 = 74HC595 [package="DIP16 [THT]"]
  R57 = Resistor [tolerance=±5% resistance=1k package=THT]
  R58 = Resistor [tolerance=±5% resistance=1k package=THT]
  R59 = Resistor [tolerance=±5% resistance=1k package=THT]
  R60 = Resistor [tolerance=±5% resistance=1k package=THT]
  R62 = Resistor [tolerance=±5% resistance=1k package=THT]
  R64 = Resistor [tolerance=±5% resistance=1k package=THT]
  R66 = Resistor [tolerance=±5% resistance=1k package=THT]
  R67 = Resistor [tolerance=±5% resistance=1k package=THT]
  R69 = Resistor [tolerance=±5% resistance=1k package=THT]
  R70 = Resistor [tolerance=±5% resistance=1k package=THT]
  R71 = Resistor [tolerance=±5% resistance=1k package=THT]
  R72 = Resistor [tolerance=±5% resistance=1k package=THT]
  R73 = Resistor [tolerance=±5% resistance=1k package=THT]
  R74 = Resistor [tolerance=±5% resistance=1k package=THT]
  R75 = Resistor [tolerance=±5% resistance=1k package=THT]
  R76 = Resistor [tolerance=±5% resistance=1k package=THT]
  LED17 = LED - 5mm [color="Red (635nm)" package="5 mm [THT]"]

nets:
  N1: Raspberry_Pi_1.3v3, S1.Pin_3, S1.Pin_4
  N2: Raspberry_Pi_1.GPIO2, IC1.pin7
  N3: Raspberry_Pi_1.GPIO3, IC1.pin1
  N4: Raspberry_Pi_1.GPIO4, IC1.pin6
  N5: Raspberry_Pi_1.GPIO17, IC1.pin2
  GND: Raspberry_Pi_1.GPIO27, Raspberry_Pi_1.GND, U1.GND, LED1.cathode, LED2.cathode, LED3.cathode, LED4.cathode, LED5.cathode, LED6.cathode, LED7.cathode, LED8.cathode, LED9.cathode, LED10.cathode, LED11.cathode, LED12.cathode, LED13.cathode, LED14.cathode, LED15.cathode, LED16.cathode, R42.Pin_0, R42.Pin_1, IC1.pin8, S1.Pin_1, S1.Pin_2, U2.GND, LED17.cathode
  N6: Raspberry_Pi_1.GPIO22, R47.Pin_0, R47.Pin_1
  N7: Raspberry_Pi_1.GPIO13, U1.SH_CP
  N8: Raspberry_Pi_1.GPIO19, U1.ST_CP
  N9: Raspberry_Pi_1.GPIO26, U1.DS
  N10: Raspberry_Pi_1.GPIO21, U2.SH_CP
  N11: Raspberry_Pi_1.GPIO20, U2.ST_CP
  N12: Raspberry_Pi_1.GPIO16, U2.DS
  5V: Raspberry_Pi_1.5V, U1.MR, U1.VCC, R40.Pin_0, R40.Pin_1
  N13: U1.Q1, R67.Pin_0
  N14: U1.Q2, R58.Pin_0
  N15: U1.Q3, R62.Pin_0
  N16: U1.Q4, R60.Pin_0
  N17: U1.Q5, R57.Pin_0
  N18: U1.Q6, R66.Pin_0
  N19: U1.Q7, R64.Pin_0
  N20: U1.Q0, R59.Pin_0
  N21: LED1.anode, R59.Pin_1
  N22: LED2.anode, R67.Pin_1
  N23: LED3.anode, R58.Pin_1
  N24: LED4.anode, R62.Pin_1
  N25: LED5.anode, R60.Pin_1
  N26: LED6.anode, R73.Pin_1
  N27: LED7.anode, R72.Pin_1
  N28: LED8.anode, R70.Pin_1
  N29: LED9.anode, R71.Pin_1
  N30: LED10.anode, R76.Pin_1
  N31: LED11.anode, R57.Pin_1
  N32: LED12.anode, R66.Pin_1
  N33: LED13.anode, R69.Pin_1
  N34: LED14.anode, R75.Pin_1
  N35: LED15.anode, R64.Pin_1
  N36: LED16.anode, LED17.anode
  N37: IC1.pin16, U2.MR, U2.VCC
  N38: U2.Q1, R76.Pin_0
  N39: U2.Q2, R70.Pin_0
  N40: U2.Q3, R73.Pin_0
  N41: U2.Q4, R72.Pin_0
  N42: U2.Q5, R69.Pin_0
  N43: U2.Q6, R75.Pin_0
  N44: U2.Q7, R74.Pin_0
  N45: U2.Q0, R71.Pin_0
